// Logisim project OppoT2.circ as structural Verilog: 8 circuits, main circuit main
module main (
);

  wire and_1_out, and_2_out, and_3_out, clock_1_out, comparator_1_eq, comparator_2_eq, cpu_1_memclk,
       cpu_1_memread, cpu_1_memwe, keyboard_1_avail, nor_1_out, or_1_out, priority_encoder_1_out, reset_out;
  wire [6:0] bit_extender_1_out, keyboard_1_data;
  wire [23:0] cpu_1_memaddr;
  wire [31:0] bit_extender_2_out, cpu_1_dataout, genMem_dout, multiplexer_1_out, multiplexer_2_out;
  wire [31:24] cpu_1_memaddr_2;

  and and_1 (and_1_out, cpu_1_memwe, nor_1_out);
  nor nor_1 (nor_1_out, cpu_1_memaddr_2[31], cpu_1_memaddr_2[30], cpu_1_memaddr_2[29], cpu_1_memaddr_2[28], cpu_1_memaddr_2[27], cpu_1_memaddr_2[26], cpu_1_memaddr_2[25], cpu_1_memaddr_2[24]);
  RAM #(.addrWidth(24), .dataWidth(32), .enables("line"), .\type ("nonvolatile")) genMem (
    .addr(cpu_1_memaddr), .we(and_1_out), .clk(cpu_1_memclk), .din(cpu_1_dataout), .dout(genMem_dout));
  Comparator #(.width(32)) comparator_1 (
    .a({cpu_1_memaddr_2, cpu_1_memaddr}), .b({32{1'b1}}), .eq(comparator_1_eq));  // open: gt, lt
  Comparator #(.width(32)) comparator_2 (
    .a({cpu_1_memaddr_2, cpu_1_memaddr}), .b(32'hfffffffe), .eq(comparator_2_eq));  // open: gt, lt
  Clock clock_1 (.out(clock_1_out));
  Bit_Extender #(.in_width(32), .out_width(7), .\type ("zero")) bit_extender_1 (
    .in(cpu_1_dataout), .out(bit_extender_1_out));
  and and_2 (and_2_out, comparator_2_eq, cpu_1_memread);
  Multiplexer #(.width(32)) multiplexer_1 (
    .in0(genMem_dout), .in1(bit_extender_2_out), .out(multiplexer_1_out), .sel(comparator_2_eq));
  TTY tty_1 (.data(bit_extender_1_out), .clk(cpu_1_memclk), .we(and_3_out));  // open: clr
  and and_3 (and_3_out, comparator_1_eq, cpu_1_memwe);
  Keyboard keyboard_1 (
    .clk(cpu_1_memclk), .re(and_2_out), .avail(keyboard_1_avail), .data(keyboard_1_data));  // open: clr
  assign bit_extender_2_out = {{25{1'b0}}, keyboard_1_data};  // Bit_Extender bit_extender_2
  CPU cpu_1 (
    .dataIN(multiplexer_1_out), .interruptSTATUS(multiplexer_2_out), .intREQ(or_1_out), .cpuCLK(clock_1_out),
    .dataOUT(cpu_1_dataout), .memADDR({cpu_1_memaddr_2, cpu_1_memaddr}), .memCLK(cpu_1_memclk),
    .memWE(cpu_1_memwe), .memREAD(cpu_1_memread));
  Button reset (.out(reset_out));
  or or_1 (or_1_out, keyboard_1_avail, reset_out);
  Multiplexer #(.width(32)) multiplexer_2 (
    .in0(32'hf000000), .in1(32'h1f000000), .out(multiplexer_2_out), .sel(priority_encoder_1_out));
  Priority_Encoder #(.select(1)) priority_encoder_1 (
    .in0(keyboard_1_avail), .in1(reset_out), .out(priority_encoder_1_out), .en_in(or_1_out));  // open: gs, en_out

  // Notes on the sheet:
  //   keyboard
  //   soft reset
endmodule

module CPU (
  input  [31:0] dataIN,
  input  [31:0] interruptSTATUS,
  input  intREQ,
  input  cpuCLK,
  output [31:0] dataOUT,
  output [31:0] memADDR,
  output memWE,
  output memREAD,
  output memCLK
);

  wire and_1_out, and_2_out, and_3_out, and_4_out, and_5_out, and_6_out, and_7_out, and_8_out, and_9_out,
       buffer_1_out, csrWE, cuCOND, d_ff_1_qn, d_ff_2_qn, d_ff_3_qn, d_ff_4_qn, d_ff_5_qn, d_ff_6_qn,
       d_ff_7_qn, d_ff_8_qn, decodeCLK, interrupthandler_1_intact, intPC, intRF, muxIntPC, muxRF, muxSIRA,
       muxSRC1, muxSRC2, or_1_out, or_2_out, or_3_out, or_4_out, or_5_out, pcCLK, pcIMMED, pcMUX, resumeCLK,
       rfCLK, rfCSR, rfWE, saveCONTROL, setORI, stackFUNC, stackOP, t_ff_1_q, t_ff_2_q, writeISR;
  wire [1:0] muxWB;
  wire [2:0] aluCOND, aluFUNC;
  wire [4:0] controlunit_1_ra, controlunit_1_rb, controlunit_1_rc, multiplexer_4_out, multiplexer_5_out,
       multiplexer_6_out;
  wire [31:0] alu_1_aluout, controlunit_1_imm15, controlunit_1_simm13, controlunit_1_simm17, CSR,
       interrupthandler_1_intstatusout, multiplexer_1_out, multiplexer_3_out, multiplexer_7_out,
       multiplexer_8_out, multiplexer_9_out, multiplexer_10_out, multiplexer_11_out, pc_1_intpcret,
       pc_1_pcjarl, pc_1_pcout, regfile_1_src1out, register_1_q;

  and and_1 (and_1_out, pcCLK, ~saveCONTROL);  // AND_Gate
  Multiplexer #(.width(32)) multiplexer_1 (
    .in0(alu_1_aluout), .in1(regfile_1_src1out), .out(multiplexer_1_out), .sel(stackFUNC));
  Multiplexer #(.width(32)) multiplexer_2 (.in0(multiplexer_1_out), .in1(pc_1_pcout), .out(memADDR), .sel(pcCLK));
  and and_2 (and_2_out, cpuCLK, ~t_ff_2_q);  // AND_Gate
  Register #(.width(32)) u_csr (.D(dataOUT), .en(csrWE), .Q(CSR), .clk(rfCLK));  // open: clr
  or or_1 (or_1_out, muxIntPC, pcMUX);
  or or_2 (or_2_out, intRF, and_1_out);
  LED decode (.in(decodeCLK));
  or or_3 (or_3_out, and_4_out, and_3_out);
  and and_3 (and_3_out, d_ff_1_qn, d_ff_2_qn, d_ff_3_qn, d_ff_4_qn);
  and and_4 (and_4_out, d_ff_1_qn, d_ff_2_qn, d_ff_3_qn, ~d_ff_4_qn);  // AND_Gate
  Multiplexer #(.width(32)) multiplexer_3 (.in0(alu_1_aluout), .in1(32'h1fff), .out(multiplexer_3_out));  // open: sel
  LED registerWrite (.in(rfCLK));
  D_Flip_Flop d_ff_1 (.clk(and_2_out), .D(or_3_out), .Q(decodeCLK), .Qn(d_ff_1_qn));  // open: preset, reset
  T_Flip_Flop t_ff_1 (.Q(t_ff_1_q), .preset(saveCONTROL), .reset(CSR[31]));  // open: clk, T, Qn
  PC pc_1 (
    .aluIN(multiplexer_3_out), .pcCLK(or_2_out), .pcMUX(or_1_out), .immedIN(controlunit_1_simm13),
    .pcIMMED(pcIMMED), .savePC(intPC), .pcOUT(pc_1_pcout), .pcJARL(pc_1_pcjarl), .intPCRET(pc_1_intpcret));
  D_Flip_Flop d_ff_2 (.clk(and_2_out), .D(decodeCLK), .Q(rfCLK), .Qn(d_ff_2_qn));  // open: preset, reset
  and and_5 (and_5_out, intREQ, ~t_ff_1_q);  // AND_Gate
  and and_6 (and_6_out, and_5_out, ~CSR[31]);  // AND_Gate
  LED memWrite (.in(memCLK));
  D_Flip_Flop d_ff_3 (.clk(and_2_out), .D(rfCLK), .Q(memCLK), .Qn(d_ff_3_qn));  // open: preset, reset
  LED PCInc (.in(pcCLK));
  D_Flip_Flop d_ff_4 (.clk(and_2_out), .D(memCLK), .Q(pcCLK), .Qn(d_ff_4_qn));  // open: preset, reset
  and and_7 (and_7_out, cpuCLK, t_ff_2_q);
  InterruptHandler interrupthandler_1 (
    .intSTATUS(interruptSTATUS), .intCLK(cpuCLK), .intREQ(and_6_out), .intACK(resumeCLK),
    .intACT(interrupthandler_1_intact), .intSTATUSOUT(interrupthandler_1_intstatusout));
  Register #(.width(32)) register_1 (.D(dataIN), .Q(register_1_q), .clk(decodeCLK));  // open: en, clr
  LED intSAVE (.in(saveCONTROL));
  or or_4 (or_4_out, and_9_out, and_8_out);
  and and_8 (and_8_out, d_ff_5_qn, d_ff_6_qn, d_ff_7_qn, d_ff_8_qn);
  and and_9 (and_9_out, d_ff_5_qn, d_ff_6_qn, d_ff_7_qn, ~d_ff_8_qn);  // AND_Gate
  ControlUnit controlunit_1 (
    .handleINT(writeISR), .aluCOND(cuCOND), .instructionIN(register_1_q), .simm13(controlunit_1_simm13),
    .imm15(controlunit_1_imm15), .simm17(controlunit_1_simm17), .condOUT(aluCOND), .rA(controlunit_1_ra),
    .rB(controlunit_1_rb), .rC(controlunit_1_rc), .rfWE(rfWE), .muxSRC2(muxSRC2), .muxSRC1(muxSRC1),
    .pcMUX(pcMUX), .pcIMMED(pcIMMED), .muxRF(muxRF), .memWE(memWE), .stackOP(stackOP), .stackFUNC(stackFUNC),
    .intRESTORE(muxSIRA), .readWORD(memREAD), .setORI(setORI), .csrWE(csrWE), .rfCSR(rfCSR),
    .funcALU(aluFUNC), .muxWB(muxWB));
  D_Flip_Flop d_ff_5 (.clk(and_7_out), .D(or_4_out), .Q(saveCONTROL), .Qn(d_ff_5_qn), .reset(rfCLK));  // open: preset
  T_Flip_Flop t_ff_2 (.clk(pcCLK), .T(interrupthandler_1_intact), .Q(t_ff_2_q), .reset(resumeCLK));  // open: Qn, preset
  LED u_intPC (.in(intPC));
  D_Flip_Flop d_ff_6 (.clk(and_7_out), .D(saveCONTROL), .Q(intPC), .Qn(d_ff_6_qn), .reset(rfCLK));  // open: preset
  LED u_intRF (.in(intRF));
  D_Flip_Flop d_ff_7 (.clk(and_7_out), .D(intPC), .Q(intRF), .Qn(d_ff_7_qn), .reset(rfCLK));  // open: preset
  LED intRES (.in(resumeCLK));
  D_Flip_Flop d_ff_8 (.clk(and_7_out), .D(intRF), .Q(resumeCLK), .Qn(d_ff_8_qn), .reset(rfCLK));  // open: preset
  Multiplexer #(.width(5)) multiplexer_4 (
    .in0(controlunit_1_rc), .in1(controlunit_1_ra), .out(multiplexer_4_out), .sel(muxRF));
  Multiplexer #(.width(5)) multiplexer_5 (
    .in0(controlunit_1_ra), .in1(5'b11110), .out(multiplexer_5_out), .sel(writeISR));
  Multiplexer #(.width(5)) multiplexer_6 (
    .in0(controlunit_1_rb), .in1({5{1'b1}}), .out(multiplexer_6_out), .sel(stackFUNC));
  buf buffer_1 (buffer_1_out, or_5_out);
  or or_5 (or_5_out, rfCLK, intRF);
  T_Flip_Flop t_ff_3 (.Q(writeISR), .preset(saveCONTROL), .reset(resumeCLK));  // open: clk, T, Qn
  Multiplexer #(.select(2), .width(32)) multiplexer_7 (
    .in0(alu_1_aluout), .in1(dataIN), .in2(pc_1_pcjarl), .in3(interrupthandler_1_intstatusout),
    .out(multiplexer_7_out));  // open: sel
  Multiplexer #(.width(32)) multiplexer_8 (
    .in0(multiplexer_7_out), .in1(pc_1_intpcret), .out(multiplexer_8_out));  // open: sel
  Multiplexer #(.width(32)) multiplexer_9 (.in0(multiplexer_8_out), .in1(CSR), .out(multiplexer_9_out));  // open: sel
  Multiplexer #(.width(32)) multiplexer_10 (
    .in0(dataOUT), .in1(controlunit_1_simm17), .out(multiplexer_10_out));  // open: sel
  T_Flip_Flop t_ff_4 (.Q(muxIntPC), .preset(saveCONTROL), .reset(resumeCLK));  // open: clk, T, Qn
  RegFile regfile_1 (
    .rfWE(rfWE), .dataIN(multiplexer_9_out), .clk(buffer_1_out), .tgt(multiplexer_5_out),
    .src1(multiplexer_6_out), .src2(multiplexer_4_out), .stackFUNC(stackFUNC), .stackOP(stackOP),
    .src1OUT(regfile_1_src1out), .src2OUT(dataOUT));
  Multiplexer #(.width(32)) multiplexer_11 (
    .in0(regfile_1_src1out), .in1(controlunit_1_imm15), .out(multiplexer_11_out));  // open: sel
  ALU alu_1 (
    .ori(setORI), .src1(multiplexer_11_out), .src2(multiplexer_10_out), .aluCOND(aluCOND), .aluFUNC(aluFUNC),
    .aluOUT(alu_1_aluout), .condOUT(cuCOND));

  // Notes on the sheet:
  //   isr handler mem location
  //   normal clk
  //   Handles functionality of int clk
  //   Handles when the CPU accepts an interrupt
  //   int clk
  //   tgt = isr
  //   the control lines to change during saveCONTROL
endmodule

module ALU (
  input  [2:0] aluFUNC,
  input  [31:0] src1,
  input  [31:0] src2,
  input  ori,
  input  [2:0] aluCOND,
  output [31:0] aluOUT,
  output condOUT
);

  wire comparator_1_eq, comparator_1_gt, comparator_1_lt, not_1_out, not_2_out, or_2_out, or_3_out, or_4_out;
  wire [16:0] bit_extender_1_out;
  wire [31:0] adder_1_out, and_1_out, bit_extender_2_out, multiplexer_1_out, negator_1_out, or_1_out,
       shifter_1_out, shifter_2_out, xor_1_out;

  Bit_Extender #(.in_width(32), .out_width(17), .\type ("zero")) bit_extender_1 (.in(src2), .out(bit_extender_1_out));
  assign bit_extender_2_out = {{15{1'b0}}, bit_extender_1_out};  // Bit_Extender bit_extender_2
  Multiplexer #(.width(32)) multiplexer_1 (.in0(src2), .in1(bit_extender_2_out), .out(multiplexer_1_out), .sel(ori));
  Adder #(.width(32)) adder_1 (.a(src1), .b(multiplexer_1_out), .out(adder_1_out));  // open: cin, cout
  assign and_1_out = src1 & multiplexer_1_out;  // AND_Gate and_1, 32 bits wide
  assign or_1_out = src1 | multiplexer_1_out;  // OR_Gate or_1, 32 bits wide
  assign xor_1_out = src1 ^ multiplexer_1_out;  // XOR_Gate xor_1, 32 bits wide
  Shifter #(.width(32)) shifter_1 (.in(src1), .\dist (multiplexer_1_out[4:0]), .out(shifter_1_out));
  Shifter #(.shift("lr"), .width(32)) shifter_2 (.in(src1), .\dist (multiplexer_1_out[4:0]), .out(shifter_2_out));
  Negator #(.width(32)) negator_1 (.in(src1), .out(negator_1_out));
  Comparator #(.width(32)) comparator_1 (
    .a(src1), .b(multiplexer_1_out), .gt(comparator_1_gt), .eq(comparator_1_eq), .lt(comparator_1_lt));
  Multiplexer #(.select(3), .width(32)) multiplexer_2 (
    .in0(adder_1_out), .in1(and_1_out), .in2(or_1_out), .in3(xor_1_out), .in4(shifter_1_out),
    .in5(shifter_2_out), .in6(negator_1_out), .in7(src1), .out(aluOUT));  // open: sel
  not not_1 (not_1_out, comparator_1_eq);
  or or_2 (or_2_out, comparator_1_gt, comparator_1_eq);
  or or_3 (or_3_out, comparator_1_lt, comparator_1_eq);
  not not_2 (not_2_out, or_3_out);
  or or_4 (or_4_out, not_2_out, or_3_out);
  Multiplexer #(.select(3)) multiplexer_3 (
    .in0(comparator_1_eq), .in1(not_1_out), .in2(comparator_1_gt), .in3(or_2_out), .in4(comparator_1_lt),
    .in5(or_3_out), .in6(or_4_out), .out(condOUT), .sel(aluCOND));  // open: in7
endmodule

module RegFile (
  input  [31:0] dataIN,
  input  clk,
  input  [4:0] tgt,
  input  rfWE,
  input  [4:0] src1,
  input  [4:0] src2,
  input  stackFUNC,
  input  stackOP,
  output [31:0] src1OUT,
  output [31:0] src2OUT
);

  wire decoder_1_out1, decoder_1_out2, decoder_1_out3, decoder_1_out4, decoder_1_out5, decoder_1_out6,
       decoder_1_out7, decoder_1_out8, decoder_1_out9, decoder_1_out10, decoder_1_out11, decoder_1_out12,
       decoder_1_out13, decoder_1_out14, decoder_1_out15, decoder_1_out16, decoder_1_out17, decoder_1_out18,
       decoder_1_out19, decoder_1_out20, decoder_1_out21, decoder_1_out22, decoder_1_out23, decoder_1_out24,
       decoder_1_out25, decoder_1_out26, decoder_1_out27, decoder_1_out28, decoder_1_out29, decoder_1_out30,
       decoder_1_out31, or_1_out;
  wire [31:0] adder_1_out, f0_q, isr_q, multiplexer_1_out, multiplexer_2_out, r19_q, r20_q, r21_q, r22_q,
       r23_q, r24_q, r25_q, r26_q, r27_q, r28_q, r29_q, retAddr_q, s0_q, s1_q, s2_q, s3_q, s4_q, s5_q, s6_q,
       s7_q, sp_q, subtractor_1_out, t0_q, t1_q, t2_q, t3_q, t4_q, t5_q, t6_q, t7_q;

  Decoder #(.select(5)) decoder_1 (
    .out1(decoder_1_out1), .out2(decoder_1_out2), .out3(decoder_1_out3), .out4(decoder_1_out4),
    .out5(decoder_1_out5), .out6(decoder_1_out6), .out7(decoder_1_out7), .out8(decoder_1_out8),
    .out9(decoder_1_out9), .out10(decoder_1_out10), .out11(decoder_1_out11), .out12(decoder_1_out12),
    .out13(decoder_1_out13), .out14(decoder_1_out14), .out15(decoder_1_out15), .out16(decoder_1_out16),
    .out17(decoder_1_out17), .out18(decoder_1_out18), .out19(decoder_1_out19), .out20(decoder_1_out20),
    .out21(decoder_1_out21), .out22(decoder_1_out22), .out23(decoder_1_out23), .out24(decoder_1_out24),
    .out25(decoder_1_out25), .out26(decoder_1_out26), .out27(decoder_1_out27), .out28(decoder_1_out28),
    .out29(decoder_1_out29), .out30(decoder_1_out30), .out31(decoder_1_out31), .sel(tgt), .en(rfWE));  // open: out0
  Register #(.width(32)) s6 (.D(dataIN), .en(decoder_1_out8), .Q(s6_q), .clk(clk));  // open: clr
  Register #(.width(32)) t6 (.D(dataIN), .en(decoder_1_out16), .Q(t6_q), .clk(clk));  // open: clr
  Register #(.width(32)) r24 (.D(dataIN), .en(decoder_1_out24), .Q(r24_q), .clk(clk));  // open: clr
  Register #(.width(32)) retAddr (.D(dataIN), .en(decoder_1_out1), .Q(retAddr_q), .clk(clk));  // open: clr
  Register #(.width(32)) s7 (.D(dataIN), .en(decoder_1_out9), .Q(s7_q), .clk(clk));  // open: clr
  Register #(.width(32)) t7 (.D(dataIN), .en(decoder_1_out17), .Q(t7_q), .clk(clk));  // open: clr
  Register #(.width(32)) r25 (.D(dataIN), .en(decoder_1_out25), .Q(r25_q), .clk(clk));  // open: clr
  Register #(.width(32)) s0 (.D(dataIN), .en(decoder_1_out2), .Q(s0_q), .clk(clk));  // open: clr
  Register #(.width(32)) t0 (.D(dataIN), .en(decoder_1_out10), .Q(t0_q), .clk(clk));  // open: clr
  Register #(.width(32)) f0 (.D(dataIN), .en(decoder_1_out18), .Q(f0_q), .clk(clk));  // open: clr
  Register #(.width(32)) r26 (.D(dataIN), .en(decoder_1_out26), .Q(r26_q), .clk(clk));  // open: clr
  Register #(.width(32)) s1 (.D(dataIN), .en(decoder_1_out3), .Q(s1_q), .clk(clk));  // open: clr
  Register #(.width(32)) t1 (.D(dataIN), .en(decoder_1_out11), .Q(t1_q), .clk(clk));  // open: clr
  Register #(.width(32)) r19 (.D(dataIN), .en(decoder_1_out19), .Q(r19_q), .clk(clk));  // open: clr
  Register #(.width(32)) r27 (.D(dataIN), .en(decoder_1_out27), .Q(r27_q), .clk(clk));  // open: clr
  Register #(.width(32)) s2 (.D(dataIN), .en(decoder_1_out4), .Q(s2_q), .clk(clk));  // open: clr
  Register #(.width(32)) t2 (.D(dataIN), .en(decoder_1_out12), .Q(t2_q), .clk(clk));  // open: clr
  Register #(.width(32)) r20 (.D(dataIN), .en(decoder_1_out20), .Q(r20_q), .clk(clk));  // open: clr
  Register #(.width(32)) r28 (.D(dataIN), .en(decoder_1_out28), .Q(r28_q), .clk(clk));  // open: clr
  Subtractor #(.width(32)) subtractor_1 (.a(sp_q), .b(32'h1), .out(subtractor_1_out));  // open: bin, bout
  Adder #(.width(32)) adder_1 (.a(sp_q), .b(32'h1), .out(adder_1_out));  // open: cin, cout
  Register #(.width(32)) s3 (.D(dataIN), .en(decoder_1_out5), .Q(s3_q), .clk(clk));  // open: clr
  Register #(.width(32)) t3 (.D(dataIN), .en(decoder_1_out13), .Q(t3_q), .clk(clk));  // open: clr
  Register #(.width(32)) r21 (.D(dataIN), .en(decoder_1_out21), .Q(r21_q), .clk(clk));  // open: clr
  Register #(.width(32)) r29 (.D(dataIN), .en(decoder_1_out29), .Q(r29_q), .clk(clk));  // open: clr
  Multiplexer #(.width(32)) multiplexer_1 (
    .in0(dataIN), .in1(multiplexer_2_out), .out(multiplexer_1_out), .sel(stackFUNC));
  Multiplexer #(.width(32)) multiplexer_2 (
    .in0(subtractor_1_out), .in1(adder_1_out), .out(multiplexer_2_out), .sel(stackOP));
  or or_1 (or_1_out, decoder_1_out31, stackFUNC);
  Register #(.width(32)) s4 (.D(dataIN), .en(decoder_1_out6), .Q(s4_q), .clk(clk));  // open: clr
  Register #(.width(32)) t4 (.D(dataIN), .en(decoder_1_out14), .Q(t4_q), .clk(clk));  // open: clr
  Register #(.width(32)) r22 (.D(dataIN), .en(decoder_1_out22), .Q(r22_q), .clk(clk));  // open: clr
  Register #(.width(32)) isr (.D(dataIN), .en(decoder_1_out30), .Q(isr_q), .clk(clk));  // open: clr
  Register #(.width(32)) sp (.D(multiplexer_1_out), .en(or_1_out), .Q(sp_q), .clk(clk));  // open: clr
  Register #(.width(32)) s5 (.D(dataIN), .en(decoder_1_out7), .Q(s5_q), .clk(clk));  // open: clr
  Register #(.width(32)) t5 (.D(dataIN), .en(decoder_1_out15), .Q(t5_q), .clk(clk));  // open: clr
  Register #(.width(32)) r23 (.D(dataIN), .en(decoder_1_out23), .Q(r23_q), .clk(clk));  // open: clr
  Multiplexer #(.select(5), .width(32)) multiplexer_3 (
    .in0({32{1'b0}}), .in1(retAddr_q), .in2(s0_q), .in3(s1_q), .in4(s2_q), .in5(s3_q), .in6(s4_q),
    .in7(s5_q), .in8(s6_q), .in9(s7_q), .in10(t0_q), .in11(t1_q), .in12(t2_q), .in13(t3_q), .in14(t4_q),
    .in15(t5_q), .in16(t6_q), .in17(t7_q), .in18(f0_q), .in19(r19_q), .in20(r20_q), .in21(r21_q),
    .in22(r22_q), .in23(r23_q), .in24(r24_q), .in25(r25_q), .in26(r26_q), .in27(r27_q), .in28(r28_q),
    .in29(r29_q), .in30(isr_q), .in31(sp_q), .out(src1OUT));  // open: sel
  Multiplexer #(.select(5), .width(32)) multiplexer_4 (
    .in0({32{1'b0}}), .in1(retAddr_q), .in2(s0_q), .in3(s1_q), .in4(s2_q), .in5(s3_q), .in6(s4_q),
    .in7(s5_q), .in8(s6_q), .in9(s7_q), .in10(t0_q), .in11(t1_q), .in12(t2_q), .in13(t3_q), .in14(t4_q),
    .in15(t5_q), .in16(t6_q), .in17(t7_q), .in18(f0_q), .in19(r19_q), .in20(r20_q), .in21(r21_q),
    .in22(r22_q), .in23(r23_q), .in24(r24_q), .in25(r25_q), .in26(r26_q), .in27(r27_q), .in28(r28_q),
    .in29(r29_q), .in30(isr_q), .in31(sp_q), .out(src2OUT));  // open: sel

  // Notes on the sheet:
  //   zero
  //   push = decrement
endmodule

module PC (
  input  [31:0] aluIN,
  input  pcCLK,
  input  pcMUX,
  input  [31:0] immedIN,
  input  pcIMMED,
  input  savePC,
  output [31:0] pcOUT,
  output [31:0] pcJARL,
  output [31:0] intPCRET
);

  wire and_1_out, buffer_1_out;
  wire [31:0] multiplexer_1_out, multiplexer_2_out;

  Multiplexer #(.width(32)) multiplexer_1 (.in0(pcJARL), .in1(aluIN), .out(multiplexer_1_out), .sel(pcMUX));
  buf buffer_1 (buffer_1_out, savePC);
  and and_1 (and_1_out, pcCLK, ~savePC);  // AND_Gate
  Register #(.width(32)) register_1 (.D(pcOUT), .en(savePC), .Q(intPCRET), .clk(buffer_1_out));  // open: clr
  Register #(.width(32)) register_2 (.D(multiplexer_1_out), .Q(pcOUT), .clk(and_1_out));  // open: en, clr
  Multiplexer #(.width(32)) multiplexer_2 (.in0(32'h1), .in1(immedIN), .out(multiplexer_2_out), .sel(pcIMMED));
  Adder #(.width(32)) adder_1 (.a(pcOUT), .b(multiplexer_2_out), .out(pcJARL), .cin(pcIMMED));  // open: cout
endmodule

module StackLogic (
  input  [31:0] stackADDR,
  input  stackFunc,
  input  stackOperation,
  input  clk,
  input  stackWE,
  output [31:0] stackPointer
);

  wire [31:0] adder_1_out, adder_2_out, multiplexer_1_out, multiplexer_2_out, sp_q, subtractor_1_out;

  Subtractor #(.width(32)) subtractor_1 (.a(sp_q), .b(32'h1), .out(subtractor_1_out));  // open: bin, bout
  Adder #(.width(32)) adder_1 (.a(sp_q), .b(32'h1), .out(adder_1_out));  // open: cin, cout
  Multiplexer #(.width(32)) multiplexer_1 (
    .in0(subtractor_1_out), .in1(adder_1_out), .out(multiplexer_1_out), .sel(stackOperation));
  Multiplexer #(.width(32)) multiplexer_2 (
    .in0(stackADDR), .in1(multiplexer_1_out), .out(multiplexer_2_out), .sel(stackFunc));
  Register #(.width(32)) sp (.D(multiplexer_2_out), .en(stackWE), .Q(sp_q), .clk(clk));  // open: clr
  Adder #(.width(32)) adder_2 (.a(sp_q), .b(32'h1), .out(adder_2_out));  // open: cin, cout
  Multiplexer #(.width(32)) multiplexer_3 (.in0(adder_2_out), .in1(sp_q), .out(stackPointer), .sel(stackOperation));
endmodule

module ControlUnit (
  input  [31:0] instructionIN,
  input  aluCOND,
  input  handleINT,
  output [31:0] simm13,
  output [31:0] imm15,
  output [31:0] simm17,
  output [2:0] condOUT,
  output [4:0] rA,
  output [4:0] rB,
  output [4:0] rC,
  output pcIMMED,
  output [2:0] funcALU,
  output rfWE,
  output muxSRC2,
  output muxSRC1,
  output pcMUX,
  output [1:0] muxWB,
  output muxRF,
  output memWE,
  output stackOP,
  output stackFUNC,
  output intRESTORE,
  output readWORD,
  output setORI,
  output csrWE,
  output rfCSR
);

  wire decoder_1_out0, decoder_1_out1, decoder_1_out2, decoder_1_out3, decoder_1_out4, decoder_1_out5,
       decoder_1_out6, decoder_1_out7, decoder_1_out9, decoder_1_out10, decoder_1_out12, decoder_1_out16,
       decoder_1_out20, decoder_1_out21, decoder_1_out22, decoder_1_out23, decoder_1_out24, decoder_1_out25,
       decoder_1_out26, decoder_1_out27, decoder_1_out28, decoder_1_out29, decoder_1_out30, decoder_1_out31,
       or_1_out, or_2_out, or_3_out, or_4_out;

  LED add (.in(decoder_1_out0));
  LED addi (.in(decoder_1_out1));
  LED orOp (.in(decoder_1_out2));
  LED xorOp (.in(decoder_1_out3));
  LED shll (.in(decoder_1_out4));
  LED shlr (.in(decoder_1_out5));
  LED neg (.in(decoder_1_out6));
  LED andOp (.in(decoder_1_out7));
  LED lw (.in(readWORD));
  LED sw (.in(decoder_1_out9));
  LED brc (.in(decoder_1_out10));
  LED jalr (.in(pcMUX));
  LED push (.in(decoder_1_out12));
  LED pop (.in(stackOP));
  LED lui (.in(muxSRC1));
  LED sira (.in(intRESTORE));
  LED led_1 (.in(decoder_1_out16));
  LED ori (.in(setORI));
  LED csrw (.in(csrWE));
  LED csrr (.in(rfCSR));
  LED led_2 (.in(decoder_1_out20));
  LED led_3 (.in(decoder_1_out21));
  LED led_4 (.in(decoder_1_out22));
  LED led_5 (.in(decoder_1_out23));
  LED led_6 (.in(decoder_1_out24));
  LED led_7 (.in(decoder_1_out25));
  LED led_8 (.in(decoder_1_out26));
  LED led_9 (.in(decoder_1_out27));
  LED led_10 (.in(decoder_1_out28));
  LED led_11 (.in(decoder_1_out29));
  LED led_12 (.in(decoder_1_out30));
  LED led_13 (.in(decoder_1_out31));
  Hex_Digit_Display instU (.value({3'b000, instructionIN[31]}));  // open: dp
  Hex_Digit_Display instL (.value(instructionIN[30:27]));  // open: dp
  Decoder #(.enable("false"), .select(5)) decoder_1 (
    .out0(decoder_1_out0), .out1(decoder_1_out1), .out2(decoder_1_out2), .out3(decoder_1_out3),
    .out4(decoder_1_out4), .out5(decoder_1_out5), .out6(decoder_1_out6), .out7(decoder_1_out7),
    .out8(readWORD), .out9(decoder_1_out9), .out10(decoder_1_out10), .out11(pcMUX), .out12(decoder_1_out12),
    .out13(stackOP), .out14(muxSRC1), .out15(intRESTORE), .out16(decoder_1_out16), .out17(setORI),
    .out18(csrWE), .out19(rfCSR), .out20(decoder_1_out20), .out21(decoder_1_out21), .out22(decoder_1_out22),
    .out23(decoder_1_out23), .out24(decoder_1_out24), .out25(decoder_1_out25), .out26(decoder_1_out26),
    .out27(decoder_1_out27), .out28(decoder_1_out28), .out29(decoder_1_out29), .out30(decoder_1_out30),
    .out31(decoder_1_out31), .sel(instructionIN[31:27]));
  and and_1 (pcIMMED, decoder_1_out10, aluCOND);
  or or_1 (or_1_out, decoder_1_out0, decoder_1_out1);
  or or_2 (or_2_out, muxSRC1, decoder_1_out10);
  or or_3 (or_3_out, setORI, decoder_1_out2);
  or or_4 (or_4_out, stackOP, readWORD);
  or or_5 (rfWE, setORI, decoder_1_out0, decoder_1_out1, decoder_1_out2, decoder_1_out3, decoder_1_out4, decoder_1_out5, rfCSR, decoder_1_out6, decoder_1_out7, readWORD, pcMUX, stackOP, muxSRC1, intRESTORE);
  or or_6 (muxSRC2, decoder_1_out1, setORI, decoder_1_out9);
  or or_7 (muxRF, decoder_1_out12, decoder_1_out9, decoder_1_out10, csrWE);
  or or_8 (memWE, decoder_1_out9, decoder_1_out12);
  or or_9 (stackFUNC, decoder_1_out12, stackOP);
  Priority_Encoder priority_encoder_1 (
    .in0(or_1_out), .in1(decoder_1_out7), .in2(or_3_out), .in3(decoder_1_out3), .in4(decoder_1_out4),
    .in5(decoder_1_out5), .in6(decoder_1_out6), .in7(or_2_out), .out(funcALU));  // open: en_in, gs, en_out
  or or_10 (muxWB[0], or_4_out, handleINT);
  or or_11 (muxWB[1], pcMUX, handleINT);
  Hex_Digit_Display simm13_a_1 (.value({4{instructionIN[12]}}));  // open: dp
  Hex_Digit_Display simm13_a (.value({4{instructionIN[12]}}));  // open: dp
  Hex_Digit_Display simm13_a_2 (.value({4{instructionIN[12]}}));  // open: dp
  Hex_Digit_Display simm13_a_3 (.value({4{instructionIN[12]}}));  // open: dp
  Hex_Digit_Display rAU (.value({3'b000, instructionIN[26]}));  // open: dp
  Hex_Digit_Display rAL (.value(instructionIN[25:22]));  // open: dp
  Hex_Digit_Display simm13_a_4 (.value({4{instructionIN[12]}}));  // open: dp
  Hex_Digit_Display simm13_a_5 (.value(instructionIN[11:8]));  // open: dp
  Hex_Digit_Display rBU (.value({3'b000, instructionIN[21]}));  // open: dp
  Hex_Digit_Display rBL (.value(instructionIN[20:17]));  // open: dp
  Hex_Digit_Display simm13_a_6 (.value(instructionIN[7:4]));  // open: dp
  Hex_Digit_Display simm13_a_7 (.value(instructionIN[3:0]));  // open: dp
  Hex_Digit_Display rCU (.value({3'b000, instructionIN[4]}));  // open: dp
  Hex_Digit_Display imm15_a (.value(instructionIN[14:11]));  // open: dp
  Hex_Digit_Display rCL (.value(instructionIN[3:0]));  // open: dp
  Hex_Digit_Display imm15_a_1 (.value(instructionIN[10:7]));  // open: dp
  Hex_Digit_Display imm15_a_2 (.value(instructionIN[6:3]));  // open: dp
  Hex_Digit_Display imm15_a_3 (.value({instructionIN[2:0], 1'b0}));  // open: dp
  Hex_Digit_Display imm15_a_4 (.value(4'b0000));  // open: dp
  Hex_Digit_Display imm15_a_5 (.value(4'b0000));  // open: dp
  Hex_Digit_Display imm15_a_6 (.value(4'b0000));  // open: dp
  Hex_Digit_Display imm15_a_7 (.value(4'b0000));  // open: dp
  Hex_Digit_Display simm17_a (.value({4{instructionIN[16]}}));  // open: dp
  Hex_Digit_Display simm17_a_1 (.value({4{instructionIN[16]}}));  // open: dp
  Hex_Digit_Display simm17_a_2 (.value({4{instructionIN[16]}}));  // open: dp
  Hex_Digit_Display simm17_a_3 (.value({4{instructionIN[16]}}));  // open: dp
  Hex_Digit_Display simm17_a_4 (.value(instructionIN[15:12]));  // open: dp
  Hex_Digit_Display simm17_a_5 (.value(instructionIN[11:8]));  // open: dp
  Hex_Digit_Display simm17_a_6 (.value(instructionIN[7:4]));  // open: dp
  Hex_Digit_Display simm17_a_7 (.value(instructionIN[3:0]));  // open: dp

  assign condOUT = instructionIN[16:14];
  assign imm15 = {instructionIN[14:0], {17{1'b0}}};
  assign rA = instructionIN[26:22];
  assign rB = instructionIN[21:17];
  assign rC = instructionIN[4:0];
  assign simm13 = {{20{instructionIN[12]}}, instructionIN[11:0]};
  assign simm17 = {{16{instructionIN[16]}}, instructionIN[15:0]};
endmodule

module InterruptHandler (
  input  [31:0] intSTATUS,
  input  intCLK,
  input  intREQ,
  input  intACK,
  output [31:0] intSTATUSOUT,
  output intACT
);

  wire and_1_out, comparator_1_eq, t_ff_1_q;

  and and_1 (and_1_out, intCLK, t_ff_1_q);
  T_Flip_Flop t_ff_1 (.Q(t_ff_1_q), .preset(intREQ), .reset(intACT));  // open: clk, T, Qn
  Register #(.width(32)) register_1 (
    .D(intSTATUS), .en(comparator_1_eq), .Q(intSTATUSOUT), .clk(and_1_out), .clr(intACK));
  Comparator #(.width(32)) comparator_1 (.a(intSTATUSOUT), .b({32{1'b0}}), .eq(comparator_1_eq));  // open: gt, lt
  not not_1 (intACT, comparator_1_eq);

  // Notes on the sheet:
  //   async 
endmodule
